// Logisim project somador.circ as structural Verilog: 7 circuits, main circuit Meio Somador
module Meio_Somador (
  input  A0,
  input  B0,
  output S0,
  output Co0
);

  xor xor_1 (S0, A0, B0);
  and and_1 (Co0, A0, B0);

  // Notes on the sheet:
  //   Meio somador
endmodule

module Somador_Completo (
  input  A0,
  input  B0,
  input  Ci0,
  output S0,
  output Co0
);

  wire meio_somador_1_co0, meio_somador_1_s0, meio_somador_2_co0;

  Meio_Somador meio_somador_1 (.A0(A0), .B0(B0), .S0(meio_somador_1_s0), .Co0(meio_somador_1_co0));
  Meio_Somador meio_somador_2 (.A0(meio_somador_1_s0), .B0(Ci0), .S0(S0), .Co0(meio_somador_2_co0));
  or or_1 (Co0, meio_somador_2_co0, meio_somador_1_co0);

  // Notes on the sheet:
  //   Somador Completo
endmodule

module Somador_de_4_bits (
  input  [3:0] A,
  input  Carry_in,
  input  [3:0] B,
  output [3:0] S,
  output Over_flow,
  output Carry_out
);

  wire somador_completo_1_co0, somador_completo_2_co0, somador_completo_3_co0;

  Somador_Completo somador_completo_1 (.A0(A[0]), .B0(B[0]), .Ci0(Carry_in), .S0(S[0]), .Co0(somador_completo_1_co0));
  Somador_Completo somador_completo_2 (
    .A0(A[1]), .B0(B[1]), .Ci0(somador_completo_1_co0), .S0(S[1]), .Co0(somador_completo_2_co0));
  Somador_Completo somador_completo_3 (
    .A0(A[2]), .B0(B[2]), .Ci0(somador_completo_2_co0), .S0(S[2]), .Co0(somador_completo_3_co0));
  Somador_Completo somador_completo_4 (.A0(A[3]), .B0(B[3]), .Ci0(somador_completo_3_co0), .S0(S[3]), .Co0(Carry_out));
  xor xor_1 (Over_flow, somador_completo_3_co0, Carry_out);

  // Notes on the sheet:
  //   +
endmodule

module main (
  input  Carry_In,
  input  [3:0] A,
  input  [3:0] B,
  output [3:0] S,
  output Carry_Out,
  output Over_Flow
);

  wire displaydecoder_1_p2, displaydecoder_1_p3, displaydecoder_1_p4, displaydecoder_1_p5,
       displaydecoder_1_p6, displaydecoder_1_p7, displaydecoder_1_p8, displaydecoder_2_p2,
       displaydecoder_2_p3, displaydecoder_2_p4, displaydecoder_2_p5, displaydecoder_2_p6,
       displaydecoder_2_p7, displaydecoder_2_p8, displaydecoder_3_p2, displaydecoder_3_p3,
       displaydecoder_3_p4, displaydecoder_3_p5, displaydecoder_3_p6, displaydecoder_3_p7,
       displaydecoder_3_p8;

  // DisplayDecoder displaydecoder_1: pin names not known; wires that end beside it: A, displaydecoder_1_p2, displaydecoder_1_p3, displaydecoder_1_p4, displaydecoder_1_p5, displaydecoder_1_p6, displaydecoder_1_p7, displaydecoder_1_p8
  Somador_de_4_bits somador_de_4_bits_1 (
    .A(A), .B(B), .Carry_in(Carry_In), .Carry_out(Carry_Out), .S(S), .Over_flow(Over_Flow));
  // DisplayDecoder displaydecoder_2: pin names not known; wires that end beside it: B, displaydecoder_2_p2, displaydecoder_2_p3, displaydecoder_2_p4, displaydecoder_2_p5, displaydecoder_2_p6, displaydecoder_2_p7, displaydecoder_2_p8
  _7_Segment_Display u_7_segment_display_1 (
    .g(displaydecoder_1_p8), .f(displaydecoder_1_p7), .a(displaydecoder_1_p2), .b(displaydecoder_1_p3),
    .e(displaydecoder_1_p6), .d(displaydecoder_1_p5), .c(displaydecoder_1_p4));  // open: dp
  _7_Segment_Display u_7_segment_display_2 (
    .g(displaydecoder_2_p8), .f(displaydecoder_2_p7), .a(displaydecoder_2_p2), .b(displaydecoder_2_p3),
    .e(displaydecoder_2_p6), .d(displaydecoder_2_p5), .c(displaydecoder_2_p4));  // open: dp
  // DisplayDecoder displaydecoder_3: pin names not known; wires that end beside it: S, displaydecoder_3_p2, displaydecoder_3_p3, displaydecoder_3_p4, displaydecoder_3_p5, displaydecoder_3_p6, displaydecoder_3_p7, displaydecoder_3_p8
  _7_Segment_Display u_7_segment_display_3 (
    .g(displaydecoder_3_p8), .f(displaydecoder_3_p7), .a(displaydecoder_3_p2), .b(displaydecoder_3_p3),
    .e(displaydecoder_3_p6), .d(displaydecoder_3_p5), .c(displaydecoder_3_p4));  // open: dp

  // Notes on the sheet:
  //   Calculadora de 4 bits
  //   +
endmodule

module ULA_1bit (
  input  Carry_in,
  input  A,
  input  B,
  input  Binvert,
  input  Op1,
  input  Op0,
  output Result,
  output Carry_out
);

  wire and_1_out, multiplexer_1_out, not_1_out, not_2_out, or_1_out, somador_completo_1_s0;

  not not_1 (not_1_out, B);
  Multiplexer #(.enable("false")) multiplexer_1 (.in0(B), .in1(not_1_out), .out(multiplexer_1_out), .sel(Binvert));
  and and_1 (and_1_out, A, multiplexer_1_out);
  or or_1 (or_1_out, A, multiplexer_1_out);
  not not_2 (not_2_out, A);
  Somador_Completo somador_completo_1 (
    .A0(A), .B0(multiplexer_1_out), .Ci0(Carry_in), .S0(somador_completo_1_s0), .Co0(Carry_out));
  Multiplexer #(.select(2), .enable("false")) multiplexer_2 (
    .in0(and_1_out), .in1(or_1_out), .in2(not_2_out), .in3(somador_completo_1_s0), .out(Result),
    .sel({Op1, Op0}));

  // Notes on the sheet:
  //   Binvert: pull=up
  //   ULA 1bit
endmodule

module ULA_4bit (
  input  [3:0] A,
  input  [3:0] B,
  input  [1:0] OpCode,
  input  Binvert,
  output [3:0] S,
  output C_out
);

  wire ula_1bit_1_carry_out, ula_1bit_2_carry_out, ula_1bit_3_carry_out;

  ULA_1bit ula_1bit_1 (
    .A(A[0]), .B(B[0]), .Result(S[0]), .Carry_in(Binvert), .Binvert(Binvert),
    .Carry_out(ula_1bit_1_carry_out), .Op1(OpCode[1]), .Op0(OpCode[0]));
  ULA_1bit ula_1bit_2 (
    .A(A[1]), .B(B[1]), .Result(S[1]), .Carry_in(ula_1bit_1_carry_out), .Binvert(Binvert),
    .Carry_out(ula_1bit_2_carry_out), .Op1(OpCode[1]), .Op0(OpCode[0]));
  ULA_1bit ula_1bit_3 (
    .A(A[2]), .B(B[2]), .Result(S[2]), .Carry_in(ula_1bit_2_carry_out), .Binvert(Binvert),
    .Carry_out(ula_1bit_3_carry_out), .Op1(OpCode[1]), .Op0(OpCode[0]));
  ULA_1bit ula_1bit_4 (
    .A(A[3]), .B(B[3]), .Result(S[3]), .Carry_in(ula_1bit_3_carry_out), .Binvert(Binvert), .Carry_out(C_out),
    .Op1(OpCode[1]), .Op0(OpCode[0]));

  // Notes on the sheet:
  //   ULA 4bit
  //   C_in
  //   C_OUT
  //   C_OUT
  //   C_OUT
endmodule

module ULA_74LS181 (
  input  [3:0] A,
  input  [3:0] B,
  input  [3:0] in_3,
  output [3:0] out_4
);

  wire [3:0] and_1_out, and_2_out, and_3_out, nand_1_out, nor_1_out, not_1_out, not_2_out, not_3_out,
       not_4_out, not_5_out, not_6_out, or_1_out, or_2_out, or_3_out, xnor_1_out, xor_1_out;

  assign not_1_out = ~A;  // NOT_Gate not_1, 4 bits wide
  assign not_2_out = ~B;  // NOT_Gate not_2, 4 bits wide
  assign not_3_out = ~A;  // NOT_Gate not_3, 4 bits wide
  assign not_4_out = ~B;  // NOT_Gate not_4, 4 bits wide
  assign not_5_out = ~A;  // NOT_Gate not_5, 4 bits wide
  assign nor_1_out = ~(A | B);  // NOR_Gate nor_1, 4 bits wide
  assign and_1_out = not_1_out & B;  // AND_Gate and_1, 4 bits wide
  assign nand_1_out = ~(A & B);  // NAND_Gate nand_1, 4 bits wide
  assign not_6_out = ~B;  // NOT_Gate not_6, 4 bits wide
  assign xor_1_out = A ^ B;  // XOR_Gate xor_1, 4 bits wide
  assign and_2_out = A & not_2_out;  // AND_Gate and_2, 4 bits wide
  assign or_1_out = not_3_out | B;  // OR_Gate or_1, 4 bits wide
  assign xnor_1_out = ~(A ^ B);  // XNOR_Gate xnor_1, 4 bits wide
  assign and_3_out = A & B;  // AND_Gate and_3, 4 bits wide
  assign or_2_out = A | not_4_out;  // OR_Gate or_2, 4 bits wide
  assign or_3_out = A | B;  // OR_Gate or_3, 4 bits wide
  Multiplexer #(.select(4), .width(4), .enable("false")) multiplexer_1 (
    .in0(not_5_out), .in1(nor_1_out), .in2(and_1_out), .in3(4'b0000), .in4(nand_1_out), .in5(not_6_out),
    .in6(xor_1_out), .in7(and_2_out), .in8(or_1_out), .in9(xnor_1_out), .in10(B), .in11(and_3_out),
    .in12(4'b1111), .in13(or_2_out), .in14(or_3_out), .in15(A), .out(out_4), .sel(in_3));

  // Notes on the sheet:
  //   ULA 74LS181
endmodule
